# Fritzing sketch fritzing (saved by Fritzing 0.9.3b)
breadboards: 1

parts:
  Componente1 = Arduino Uno (Rev3)
  Baixo_1 = LM35 Temperature Sensor [package="TO92 [THT]"]
  Cima_2 = LM35 Temperature Sensor [package="TO92 [THT]"]
  Cima_1 = LM35 Temperature Sensor [package="TO92 [THT]"]
  Baixo_2 = LM35 Temperature Sensor [package="TO92 [THT]"]

nets:
  N1: Componente1.A1, Baixo_1.Vout
  N2: Componente1.A2, Baixo_2.Vout
  N3: Componente1.A3, Cima_1.Vout
  N4: Componente1.A4/SDA, Cima_2.Vout
  N5: Componente1.5V, Baixo_1.+Vs, Cima_2.+Vs, Cima_1.+Vs, Baixo_2.+Vs
  GND: Componente1.GND, Baixo_1.GND, Cima_2.GND, Cima_1.GND, Baixo_2.GND
